# Fritzing sketch initial_matrix (saved by Fritzing 0.8.7b)
breadboards: 1

parts:
  Часть1 = Arduino Uno (Rev3) - ICSP
  U1 = 74HC595 [package="DIP16 [THT]"]
  U2 = 74HC595 [package="DIP16 [THT]"]
  J1 = female pin header, 5 pins [form="♀ (female)"]
  J2 = male pin header, 5 pins [form="♂ (male)"]
  J3 = female pin header, 8 pins [form="♀ (female)"]
  J4 = female pin header, 8 pins [form="♀ (female)"]

nets:
  N1: Часть1.ICSP_MOSI, Часть1.D11_PWM/MOSI, U1.DS, J1.pin2
  N2: Часть1.D8, U1.ST_CP, U2.ST_CP, J1.pin3, J2.pin3
  N3: Часть1.D13/SCK, U1.SH_CP, U2.SH_CP, J1.pin4, J2.pin4
  VCC: Часть1.5V, U1.OE, U1.VCC, U2.OE, U2.VCC, J1.pin1, J2.pin1
  GND: Часть1.GND, U1.GND, U1.MR, U2.GND, J1.pin5, J2.pin5
  N4: U1.Q1, J4.pin3
  N5: U1.Q2, J4.pin4
  N6: U1.Q3, J3.pin7
  N7: U1.Q4, J4.pin6
  N8: U1.Q5, J3.pin6
  N9: U1.Q6, J3.pin2
  N10: U1.Q7, J3.pin1
  N11: U1.Q7', U2.DS, J2.pin2
  N12: U1.Q0, J3.pin4
  N13: U2.Q1, J3.pin3
  N14: U2.Q2, J4.pin8
  N15: U2.Q3, J3.pin5
  N16: U2.Q4, J4.pin1
  N17: U2.Q5, J4.pin7
  N18: U2.Q6, J4.pin2
  N19: U2.Q7, J4.pin5
  N20: U2.Q0, J3.pin8
